// Digital circuit ALU.dig as structural Verilog
module ALU (
  input  [7:0] AC_in,
  input  [7:0] N,
  input  [2:0] SEL,
  input  DIR,
  input  CLK,
  output [7:0] AC,
  output [7:0] MQ
);

  wire [7:0] divisor_8bits_1_p3, divisor_8bits_1_p4, multiplexer_1_out, multiplexer_2_out,
       multiplicador_8bits_1_p3, multiplicador_8bits_1_p4, nand_1_s, shift_1_ac, somador_8bits_1_p4,
       subtrator_8bits_1_p3, xor_1_s;

  // somador_8bits somador_8bits_1: pin names not known; wires that end beside it: 1'b0, AC_in, N, somador_8bits_1_p4
  // subtrator_8bits subtrator_8bits_1: pin names not known; wires that end beside it: AC_in, N, subtrator_8bits_1_p3
  // multiplicador_8bits multiplicador_8bits_1: pin names not known; wires that end beside it: AC_in, N, multiplicador_8bits_1_p3, multiplicador_8bits_1_p4
  // divisor_8bits divisor_8bits_1: pin names not known; wires that end beside it: AC_in, N, divisor_8bits_1_p3, divisor_8bits_1_p4
  shift shift_1 (.AC_in(AC_in), .DIR(DIR), .AC(shift_1_ac));
  \nand  nand_1 (.A(AC_in), .B(N), .S(nand_1_s));
  \xor  xor_1 (.A(AC_in), .B(N), .S(xor_1_s));
  Multiplexer #(.Selector_Bits(3), .Bits(8)) multiplexer_1 (
    .sel(SEL), .in_0(somador_8bits_1_p4), .in_1(subtrator_8bits_1_p3), .in_2(multiplicador_8bits_1_p3),
    .in_3(divisor_8bits_1_p3), .in_4(shift_1_ac), .in_5(nand_1_s), .in_6(xor_1_s), .in_7({8{1'b0}}),
    .out(multiplexer_1_out));
  Multiplexer #(.Selector_Bits(3), .Bits(8)) multiplexer_2 (
    .sel(SEL), .in_0({8{1'b0}}), .in_1({8{1'b0}}), .in_2(multiplicador_8bits_1_p4),
    .in_3(divisor_8bits_1_p4), .in_4({8{1'b0}}), .in_5({8{1'b0}}), .in_6({8{1'b0}}), .in_7({8{1'b0}}),
    .out(multiplexer_2_out));
  // register_8bits register_8bits_1: pin names not known; wires that end beside it: multiplexer_1_out, CLK, AC
  // register_8bits register_8bits_2: pin names not known; wires that end beside it: multiplexer_2_out, CLK, MQ
endmodule
