// Digital circuit shift.dig as structural Verilog
module shift (
  input  [7:0] AC_in,
  input  DIR,
  output [7:0] AC
);

  Multiplexer #(.Bits(8)) multiplexer_1 (.sel(DIR), .in_0({AC_in[6:0], 1'b0}), .in_1({1'b0, AC_in[7:1]}), .out(AC));

  // Other names for the same wires on the sheet: AC_0 = AC_in[0]; AC_1 = AC_in[1]; AC_2 = AC_in[2]; AC_3 = AC_in[3];
  //   AC_4 = AC_in[4]; AC_5 = AC_in[5]; AC_6 = AC_in[6]; AC_7 = AC_in[7]
endmodule
